# Fritzing sketch schematic (saved by Fritzing 0.9.3b)
breadboards: 1

parts:
  S1 = Pushbutton [part_number=reset package="[THT]"]
  S2 = Pushbutton [part_number=measure package="[THT]"]
  R2 = Resistor [tolerance=±5% resistance=220 package=THT]
  Part1 = Arduino Nano (Rev3.0)
  Q1 = NPN-Transistor [package="TO92 [THT]"]
  Q2 = NPN-Transistor [package="TO92 [THT]"]
  J3 = female pin header, 4 pins [form="♀ (female)" part_number="dial i_3"]
  J4 = female pin header, 4 pins [form="♀ (female)" part_number="dial i_4"]
  J5 = female pin header, 4 pins [form="♀ (female)" part_number="dial i_5"]
  Q3 = NPN-Transistor [package="TO92 [THT]"]
  Q4 = NPN-Transistor [package="TO92 [THT]"]
  Q5 = NPN-Transistor [package="TO92 [THT]"]
  Q6 = NPN-Transistor [package="TO92 [THT]"]
  Q7 = NPN-Transistor [package="TO92 [THT]"]
  Q8 = NPN-Transistor [package="TO92 [THT]"]
  Q9 = NPN-Transistor [package="TO92 [THT]"]
  Q10 = NPN-Transistor [package="TO92 [THT]"]
  J1 = female pin header, 4 pins [form="♀ (female)"]
  J1_2 = female pin header, 4 pins [form="♀ (female)" part_number="dial i_1"]
  J2 = female pin header, 4 pins [form="♀ (female)"]
  J2_2 = female pin header, 4 pins [form="♀ (female)" part_number="dial i_2"]
  J2_3 = female pin header, 4 pins [form="♀ (female)"]
  R1 = Resistor [tolerance=±5% resistance=510 package=THT]

nets:
  N1: S1.Pin_1, S1.Pin_2, R2.Pin_1, J3.pin4, J4.pin4, J5.pin4, J1.pin4, J1_2.pin4, J2.pin4, J2_3.pin4, R1.Pin_1
  N2: S1.Pin_3, S1.Pin_4, S2.Pin_3, S2.Pin_4, R2.Pin_0, Part1.GND, Q1.E, Q2.E, J3.pin1, J4.pin1, J5.pin1, Q3.E, Q4.E, Q5.E, Q6.E, Q7.E, Q8.E, Q9.E, Q10.E, J1.pin1, J1_2.pin1, J2.pin1, J2_2.pin1, J2_3.pin1
  N3: S2.Pin_1, S2.Pin_2, Part1.D2
  N4: Part1.D3, Q10.C
  N5: Part1.D4, Q6.C
  N6: Part1.D5, Q9.C
  N7: Part1.D6, Q5.C
  N8: Part1.D7, Q8.C
  N9: Part1.D8, Q4.C
  N10: Part1.D9, Q7.C
  N11: Part1.D10, Q3.C
  N12: Part1.D11/MOSI, Q2.C
  N13: Part1.D12/MISO, Q1.C
  N14: Part1.5V, R1.Pin_0
  N15: Q1.B, J1.pin2, J1_2.pin2
  N16: Q2.B, J1.pin3, J1_2.pin3
  N17: J3.pin2, Q4.B
  N18: J3.pin3, Q8.B
  N19: J4.pin2, Q5.B
  N20: J4.pin3, Q9.B
  N21: J5.pin2, Q6.B
  N22: J5.pin3, Q10.B
  N23: Q3.B, J2.pin2, J2_2.pin2, J2_3.pin2
  N24: Q7.B, J2.pin3, J2_2.pin3, J2_3.pin3
